# Fritzing sketch led_Pot (saved by Fritzing 0.9.9b)
breadboards: 1

parts:
  Componente1 = Adafruit HUZZAH32 ESP32 Feather [part_number="Adafruit #3405"]
  R3 = Rotary Potentiometer (Small) [maximum_resistance=10kΩ package=THT]

nets:
  N1: Componente1.A5_IO4, R3.wiper
  N2: Componente1.GND, R3.leg1
  N3: Componente1.3.3V, R3.leg2
