# Fritzing sketch led_RGB (saved by Fritzing 0.9.9b)
breadboards: 1

parts:
  Componente1 = Adafruit HUZZAH32 ESP32 Feather [part_number="Adafruit #3405"]
  LED1 = RGB LED (com. cathode, rgb) [package="5 mm [THT]"]
  R2 = Resistor [tolerance=±5% resistance=220 package=THT]
  R3 = Resistor [tolerance=±5% resistance=220 package=THT]
  R4 = Resistor [tolerance=±5% resistance=220 package=THT]

nets (from the breadboard view):
  N1: Componente1.GND, LED1.common_cathode
  N2: Componente1.IO12_A11, R2.Pin_0
  N3: Componente1.IO32_A7, R3.Pin_0
  N4: Componente1.IO14_A6, R4.Pin_0
  N5: LED1.red_anode, R2.Pin_1
  N6: LED1.green_anode, R3.Pin_1
  N7: LED1.blue_anode, R4.Pin_1

custom parts:
  RGB LED (com. cathode, rgb): A 5mm tri-color LED with red, green and blue inside.
