# Fritzing sketch led_RGB_accelerometro (saved by Fritzing 0.9.9b)
breadboards: 1

parts:
  Componente1 = Adafruit HUZZAH32 ESP32 Feather [part_number="Adafruit #3405"]
  LED1 = RGB LED (com. cathode, rgb) [package="5 mm [THT]"]
  R2 = Resistor [tolerance=±5% resistance=220 package=THT]
  R3 = Resistor [tolerance=±5% resistance=220 package=THT]
  R4 = Resistor [tolerance=±5% resistance=220 package=THT]
  Componente2 = Adafruit ADXL345 [part_number="Adafruit #1231"]

nets (from the breadboard view):
  N1: Componente1.IO21, Componente2.SDA/SDIO
  GND: Componente1.GND, LED1.common_cathode, Componente2.GND
  3.3V: Componente1.3.3V, Componente2.VIN
  N2: Componente1.IO12_A11, R2.Pin_0
  N3: Componente1.IO15_A8, R3.Pin_0
  N4: Componente1.IO14_A6, R4.Pin_0
  N5: Componente1.SCL, Componente2.SCL
  N6: LED1.red_anode, R2.Pin_1
  N7: LED1.green_anode, R3.Pin_1
  N8: LED1.blue_anode, R4.Pin_1

custom parts:
  RGB LED (com. cathode, rgb): A 5mm tri-color LED with red, green and blue inside.
  Adafruit ADXL345: Filling out our accelerometer offerings, we now have the really lovely digital ADXL345 from Analog Devices, a triple-axis accelerometer with digital I2C and SPI interface breakout. We added an on-board 3.3V regulator and logic-level shifting circuitry, making it a perfect choice for interfacing with any 3V or 5V microcontroller such as the Arduino. The sensor has three axes of measurements, X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
