# Fritzing sketch led_RGB_bme280 (saved by Fritzing 0.9.9b)
breadboards: 1

parts:
  Componente1 = Adafruit HUZZAH32 ESP32 Feather [part_number="Adafruit #3405"]
  LED1 = RGB LED (com. cathode, rgb) [package="5 mm [THT]"]
  R2 = Resistor [tolerance=±5% resistance=220 package=THT]
  R3 = Resistor [tolerance=±5% resistance=220 package=THT]
  R4 = Resistor [tolerance=±5% resistance=220 package=THT]
  Componente2 = Adafruit BME280

nets (from the breadboard view):
  GND: Componente1.GND, LED1.common_cathode, Componente2.GND
  3.3V: Componente1.3.3V, Componente2.VIN
  N1: Componente1.IO12_A11, R2.Pin_0
  N2: Componente1.IO32_A7, R3.Pin_0
  N3: Componente1.IO14_A6, R4.Pin_0
  N4: Componente1.SCL, Componente2.SCK/SCL
  N5: Componente1.SDA, Componente2.SDI/SDA
  N6: LED1.red_anode, R2.Pin_1
  N7: LED1.green_anode, R3.Pin_1
  N8: LED1.blue_anode, R4.Pin_1

custom parts:
  RGB LED (com. cathode, rgb): A 5mm tri-color LED with red, green and blue inside.
  Adafruit BME280: Bosch has stepped up their game with their new BME280 sensor, an environmental sensor with temperature, barometric pressure and humidity! This sensor is great for all sorts of weather/environmental sensing and can even be used in both I2C and SPI! This precision sensor from Bosch is the best low-cost sensing solution for measuring humidity with ±3% accuracy, barometric pressure with ±1 hPa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
