# Fritzing sketch led_bme280_pantalla (saved by Fritzing 0.9.9b)
breadboards: 1

parts:
  Componente1 = Adafruit HUZZAH32 ESP32 Feather [part_number="Adafruit #3405"]
  Componente2 = Adafruit BME280
  Componente3 = Adafruit 1.44 inch TFT Breakout [part_number="Adafruit #2088"]

nets:
  N1: Componente1.MISO, Componente3.MISO
  N2: Componente1.MOSI, Componente3.MOSI
  N3: Componente1.SCK, Componente3.SCK
  N4: Componente1.A5_IO4, Componente3.TFTDC
  GND: Componente1.GND, Componente2.GND, Componente3.GND
  VIN: Componente1.3.3V, Componente2.VIN, Componente3.VIN
  N5: Componente1.IO14_A6, Componente3.TFTCS
  N6: Componente1.SCL, Componente2.SCK/SCL
  N7: Componente1.SDA, Componente2.SDI/SDA

custom parts:
  Adafruit BME280: Bosch has stepped up their game with their new BME280 sensor, an environmental sensor with temperature, barometric pressure and humidity! This sensor is great for all sorts of weather/environmental sensing and can even be used in both I2C and SPI! This precision sensor from Bosch is the best low-cost sensing solution for measuring humidity with ±3% accuracy, barometric pressure with ±1 hPa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
  Adafruit 1.44 inch TFT Breakout: This lovely little display breakout is the best way to add a small, colorful and bright display to any project. Since the display uses 4-wire SPI to communicate and has its own pixel-addressable frame buffer, it can be used with every kind of microcontroller. Even a very small one with low memory and few pins available! The 1.44" display has 128x128 color pixels. Unlike the low cost "Nokia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
